// Digital circuit timer.dig as structural Verilog
module timer (
  input  load,
  input  set,
  input  clear,
  input  clk,
  input  counter,
  input  in_11,
  input  D3,
  input  load_2,
  input  set_2,
  input  clear_2,
  input  clk_2,
  input  D2,
  input  D1,
  input  D0,
  output out_5,
  output Overflow,
  output out_7,
  output out_8,
  output out_9,
  output out_12,
  output out_13,
  output out_14,
  output out_15,
  output out_21,
  output out_22,
  output out_24,
  output out_26
);

  wire and_3_out, and_4_out, and_5_out, and_6_out, and_7_out, and_8_out, and_9_out, multiplexer_1_out,
       multiplexer_2_out, multiplexer_3_out, multiplexer_4_out, multiplexer_5_out, multiplexer_6_out,
       multiplexer_7_out, multiplexer_8_out, multiplexer_9_out, multiplexer_10_out, multiplexer_11_out,
       multiplexer_12_out, undriven, undriven_2, xor_1_out, xor_2_out, xor_3_out, xor_4_out, xor_5_out,
       xor_6_out, xor_7_out, xor_8_out;

  // And and_1 has open pins: In_1=in_11, In_2=clk, out=open
  Multiplexer multiplexer_1 (.sel(load_2), .in_0(out_21), .in_1(D3), .out(multiplexer_1_out));
  D_FF_AS d_ff_as_1 (.Set(set_2), .D(multiplexer_1_out), .C(clk_2), .Clr(clear_2), .Q(out_21));  // open: nQ
  Multiplexer multiplexer_2 (.sel(load_2), .in_0(out_22), .in_1(D2), .out(multiplexer_2_out));
  D_FF_AS d_ff_as_2 (.Set(set_2), .D(multiplexer_2_out), .C(clk_2), .Clr(clear_2), .Q(out_22));  // open: nQ
  Multiplexer multiplexer_3 (.sel(load_2), .in_0(out_24), .in_1(D1), .out(multiplexer_3_out));
  D_FF_AS d_ff_as_3 (.Set(set_2), .D(multiplexer_3_out), .C(clk_2), .Clr(clear_2), .Q(out_24));  // open: nQ
  Multiplexer multiplexer_4 (.sel(load_2), .in_0(out_26), .in_1(D0), .out(multiplexer_4_out));
  D_FF_AS d_ff_as_4 (.Set(set_2), .D(multiplexer_4_out), .C(clk_2), .Clr(clear_2), .Q(out_26));  // open: nQ
  and and_2 (Overflow, out_5, and_3_out);
  xor xor_1 (xor_1_out, out_5, and_3_out);
  Multiplexer multiplexer_5 (.sel(load), .in_0(out_5), .in_1(xor_1_out), .out(multiplexer_5_out));
  D_FF_AS d_ff_as_5 (.Set(set), .D(multiplexer_5_out), .C(undriven), .Clr(clear), .Q(out_5));  // open: nQ
  and and_3 (and_3_out, out_7, and_4_out);
  xor xor_2 (xor_2_out, out_7, and_4_out);
  Multiplexer multiplexer_6 (.sel(load), .in_0(out_7), .in_1(xor_2_out), .out(multiplexer_6_out));
  D_FF_AS d_ff_as_6 (.Set(set), .D(multiplexer_6_out), .C(undriven), .Clr(clear), .Q(out_7));  // open: nQ
  and and_4 (and_4_out, out_8, and_5_out);
  xor xor_3 (xor_3_out, out_8, and_5_out);
  Multiplexer multiplexer_7 (.sel(load), .in_0(out_8), .in_1(xor_3_out), .out(multiplexer_7_out));
  D_FF_AS d_ff_as_7 (.Set(set), .D(multiplexer_7_out), .C(undriven), .Clr(clear), .Q(out_8));  // open: nQ
  and and_5 (and_5_out, out_9, and_6_out);
  xor xor_4 (xor_4_out, out_9, and_6_out);
  Multiplexer multiplexer_8 (.sel(load), .in_0(out_9), .in_1(xor_4_out), .out(multiplexer_8_out));
  D_FF_AS d_ff_as_8 (.Set(set), .D(multiplexer_8_out), .C(undriven), .Clr(clear), .Q(out_9));  // open: nQ
  and and_6 (and_6_out, out_12, and_7_out);
  xor xor_5 (xor_5_out, out_12, and_7_out);
  Multiplexer multiplexer_9 (.sel(load), .in_0(out_12), .in_1(xor_5_out), .out(multiplexer_9_out));
  D_FF_AS d_ff_as_9 (.Set(undriven_2), .D(multiplexer_9_out), .C(undriven), .Clr(clear), .Q(out_12));  // open: nQ
  and and_7 (and_7_out, out_13, and_8_out);
  xor xor_6 (xor_6_out, out_13, and_8_out);
  Multiplexer multiplexer_10 (.sel(load), .in_0(out_13), .in_1(xor_6_out), .out(multiplexer_10_out));
  D_FF_AS d_ff_as_10 (.Set(undriven_2), .D(multiplexer_10_out), .C(undriven), .Clr(clear), .Q(out_13));  // open: nQ
  and and_8 (and_8_out, out_14, and_9_out);
  xor xor_7 (xor_7_out, out_14, and_9_out);
  Multiplexer multiplexer_11 (.sel(load), .in_0(out_14), .in_1(xor_7_out), .out(multiplexer_11_out));
  D_FF_AS d_ff_as_11 (.Set(undriven_2), .D(multiplexer_11_out), .C(undriven), .Clr(clear), .Q(out_14));  // open: nQ
  and and_9 (and_9_out, out_15, counter);
  xor xor_8 (xor_8_out, out_15, counter);
  Multiplexer multiplexer_12 (.sel(load), .in_0(out_15), .in_1(xor_8_out), .out(multiplexer_12_out));
  D_FF_AS d_ff_as_12 (.Set(undriven_2), .D(multiplexer_12_out), .C(undriven), .Clr(clear), .Q(out_15));  // open: nQ

  // Notes on the sheet:
  //   clk_2: Hz: 2
endmodule
